# Fritzing sketch ligacao_eletrica (saved by Fritzing 1.0.6)
breadboards: 1

parts:
  CPU1 = NodeMCU WROOM ESP 32
  LCD1 = LCD screen
  LCM1602_IIC1 = LCM1602 IIC [part_number="LCM1602 IIC" chip_label="LCM1602 IIC" package="DIP (Dual Inline) [THT]"]

nets:
  N1: CPU1.pin_18, LCM1602_IIC1.GND
  VSS: LCD1.VSS, LCM1602_IIC1.VSS
  VDD: LCD1.VDD, LCM1602_IIC1.VDD
  N2: LCD1.V0, LCM1602_IIC1.V0
  N3: LCD1.RS, LCM1602_IIC1.RS
  N4: LCD1.R/W, LCM1602_IIC1.RW
  N5: LCD1.E, LCM1602_IIC1.E
  N6: LCD1.DB0, LCM1602_IIC1.D0
  N7: LCD1.DB1, LCM1602_IIC1.D1
  N8: LCD1.DB2, LCM1602_IIC1.D2
  N9: LCD1.DB3, LCM1602_IIC1.D3
  N10: LCD1.DB4, LCM1602_IIC1.D4
  N11: LCD1.DB5, LCM1602_IIC1.D5
  N12: LCD1.DB6, LCM1602_IIC1.D6
  N13: LCD1.DB7, LCM1602_IIC1.D7
  N14: LCD1.LED+, LCM1602_IIC1.A
  N15: LCD1.LED-, LCM1602_IIC1.K

custom parts:
  NodeMCU WROOM ESP 32: 30 pol Development Kit
  LCM1602 IIC: I2C-Module to use a 1602 or 2004 LCD on with the wire.h libory Serial LCD Modul
